# Fritzing sketch module Sketch (saved by Fritzing 0.9.4)
breadboards: 1

parts:
  Part1 = Arduino Mega 2560 (Rev3)
  U2 = GP-2106 [package=gp-2106]
  Part4 = Arduino Cellular Shield
  U3 = OBDII [package=obdii]
  U4 = Barometric Pressure Sensor
  Part2 = Tri-Axis Gyro Breakout - L3G4200D

nets:
  N1: Part1.D15/RX3, U2.TX
  N2: Part1.D14/TX3, U2.RX
  N3: Part1.SCL, Part2.SCL
  N4: Part1.SDA, Part2.SDA
  GND: Part1.GND, U2.GND, U2.ONOFF, Part4.GND, U3.ISOK-LINE, U4.GND, Part2.GND
  N5: Part1.D11_PWM, Part4.D8
  N6: Part1.D10_PWM, Part4.D7
  N7: Part1.IOREF, Part2.VCC
  3V3: Part1.3V3, U2.1PPS, U2.VCC
  5V: Part1.5V, U4.3.3V
  N8: Part1.VIN, Part4.VRAW, U3.BATTPOWER
  N9: Part1.D2_PWM, U4.DRDY
  N10: Part1.D50, U4.MISO
  N11: Part1.D51, U4.MOSI
  N12: Part1.D52, U4.SCK
  N13: Part1.D53, U4.CSB
